// Logisim project CO Project Final.circ as structural Verilog: 2 circuits, main circuit main
module ALU (
  input  [15:0] Input_1__DR,
  input  [15:0] Input_2__AC,
  input  [2:0] Selection_Lines,
  output [15:0] out_4
);

  wire [15:0] adder_1_out, adder_2_out, and_1_out, multiplier_1_out, or_1_out, subtractor_1_out;

  Adder #(.width(16)) adder_1 (.a(Input_1__DR), .b(Input_2__AC), .out(adder_1_out), .cin(1'b0));  // open: cout
  Subtractor #(.width(16)) subtractor_1 (
    .a(Input_1__DR), .b(Input_2__AC), .out(subtractor_1_out), .bin(1'b0));  // open: bout
  Multiplier #(.width(16)) multiplier_1 (.a(Input_1__DR), .b(Input_2__AC), .out(multiplier_1_out));  // open: cin, cout
  Adder #(.width(16)) adder_2 (.a(Input_1__DR), .b({16{1'b0}}), .out(adder_2_out), .cin(1'b1));  // open: cout
  assign or_1_out = Input_1__DR | Input_1__DR;  // OR_Gate or_1, 16 bits wide
  assign and_1_out = Input_1__DR & Input_2__AC;  // AND_Gate and_1, 16 bits wide
  Multiplexer #(.select(3), .width(16)) multiplexer_1 (
    .in1(Input_1__DR), .in2(adder_1_out), .in3(subtractor_1_out), .in4(multiplier_1_out), .in5(adder_2_out),
    .in6(or_1_out), .in7(and_1_out), .out(out_4), .sel(Selection_Lines));  // open: in0, en
endmodule

module main (
  output [2:0] out_1,
  output [2:0] out_2
);

  wire AC_load, and_1_out, and_2_out, and_3_out, and_4_out, and_5_out, and_6_out, and_7_out, and_9_out,
       and_10_out, and_11_out, and_12_out, and_13_out, and_14_out, and_15_out, and_16_out, and_17_out,
       and_18_out, and_20_out, and_21_out, and_22_out, and_23_out, and_24_out, and_25_out, and_26_out,
       and_27_out, and_28_out, and_30_out, ARLoad, B5, clock_1_out, D0, D1, D2, D3, D4, D5, D6, D6T6, D7,
       D_FF_q, DR_load, I_BIT, INC, mread, nor_1_out, not_1_out, not_2_out, not_3_out, not_4_out, not_5_out,
       or_3_out, or_4_out, or_10_out, or_11_out, or_12_out, or_13_out, pc_inc, SC_CLR, STR, T0, T1, T2, T3,
       T4, T5, T6, X0, X3, X4;
  wire [2:0] OP;
  wire [3:0] SC;
  wire [6:0] AR_q, bit_extender_1_out, bit_extender_2_out, pc_q;
  wire [11:0] IR_q;
  wire [15:0] ACt, ALU_out_4, bit_extender_3_out, bit_extender_4_out, DR_q, multiplexer_1_out, ram_1_data,
       TR_q;

  Clock clock_1 (.out(clock_1_out));
  Decoder #(.select(4)) decoder_1 (
    .out0(T0), .out1(T1), .out2(T2), .out3(T3), .out4(T4), .out5(T5), .out6(T6), .sel(SC));  // open: out7, out8, out9, out10, out11, out12, out13, out14, out15, en
  Decoder #(.select(3)) decoder_2 (
    .out0(D0), .out1(D1), .out2(D2), .out3(D3), .out4(D4), .out5(D5), .out6(D6), .out7(D7), .sel(OP));  // open: en
  not not_1 (not_1_out, SC_CLR);
  or or_1 (ARLoad, T2, T0);
  Counter #(.width(4), .max('hf)) u_SC (
    .count(not_1_out), .Q(SC), .clk(clock_1_out), .clr(D_FF_q));  // open: load, D, carry
  D_Flip_Flop D_FF (.clk(clock_1_out), .D(SC_CLR), .Q(D_FF_q));  // open: Qn, preset, en, reset
  and and_1 (and_1_out, D4, T4);
  ALU ALU (.Input_1__DR(DR_q), .Input_2__AC(ACt), .Selection_Lines(out_2), .out_4(ALU_out_4));
  Bit_Extender #(.in_width(16), .out_width(7)) bit_extender_1 (.in(multiplexer_1_out), .out(bit_extender_1_out));
  Bit_Extender #(.in_width(16), .out_width(7)) bit_extender_2 (.in(multiplexer_1_out), .out(bit_extender_2_out));
  Register #(.width(16)) AC (.D(ALU_out_4), .en(AC_load), .Q(ACt), .clk(clock_1_out));  // open: clr
  Register #(.width(16)) DR (.D(multiplexer_1_out), .en(DR_load), .Q(DR_q), .clk(clock_1_out));  // open: clr
  Register #(.width(16)) TR (.D(multiplexer_1_out), .en(1'b0), .Q(TR_q), .clk(clock_1_out));  // open: clr
  Register #(.width(7)) AR (.D(bit_extender_1_out), .en(ARLoad), .Q(AR_q), .clk(clock_1_out));  // open: clr
  Counter #(.width(7), .max('h7f)) pc (
    .load(and_1_out), .D(bit_extender_2_out), .count(pc_inc), .Q(pc_q), .clk(clock_1_out));  // open: carry, clr
  Register #(.width(16)) IR (
    .D(multiplexer_1_out), .en(T1), .Q({I_BIT, OP, IR_q[11:6], B5, IR_q[4:0]}), .clk(clock_1_out));  // open: clr
  and and_2 (and_2_out, D3, T4);
  and and_3 (and_3_out, D4, T4);
  and and_4 (and_4_out, D2, T5);
  and and_5 (and_5_out, T5, D1);
  and and_6 (and_6_out, T5, D0);
  and and_7 (and_7_out, D5, T6);
  assign bit_extender_3_out = {{9{1'b0}}, AR_q};  // Bit_Extender bit_extender_3
  RAM #(.addrWidth(7), .dataWidth(16), .bus("separate")) ram_1 (
    .addr(AR_q), .din(multiplexer_1_out), .data(ram_1_data), .str(STR), .clk(clock_1_out), .ld(mread));  // open: sel, clr
  assign bit_extender_4_out = {{9{1'b0}}, pc_q};  // Bit_Extender bit_extender_4
  Multiplexer #(.select(3), .width(16), .enable("false")) multiplexer_1 (
    .in0(ACt), .in1(DR_q), .in2(TR_q), .in3(bit_extender_3_out), .in4(ram_1_data), .in5(bit_extender_4_out),
    .in6({I_BIT, OP, IR_q[11:6], B5, IR_q[4:0]}), .out(multiplexer_1_out), .sel(out_1));  // open: in7
  or or_2 (SC_CLR, D6T6, and_2_out, and_3_out, and_4_out, and_5_out, and_6_out, and_7_out, INC);
  nor nor_1 (nor_1_out, ACt[0], ACt[1], ACt[2], ACt[3], ACt[4], ACt[5], ACt[6], ACt[7], ACt[8], ACt[9], ACt[10], ACt[11], ACt[12], ACt[13], ACt[14], ACt[15]);
  or or_3 (or_3_out, D6, D2, D1, D0, D5);
  not not_2 (not_2_out, I_BIT);
  and and_8 (D6T6, D6, T6);
  and and_9 (and_9_out, T4, D3);
  and and_10 (and_10_out, T5, D5);
  and and_11 (and_11_out, D7, T3, not_2_out, B5);
  or or_4 (or_4_out, D5, D0, D1, D2, D6);
  and and_12 (and_12_out, T6, nor_1_out, D6);
  and and_13 (and_13_out, T4, or_3_out);
  or or_5 (STR, D6T6, and_9_out);
  or or_6 (pc_inc, and_12_out, T1);
  or or_7 (DR_load, and_13_out, and_10_out, and_11_out);
  and and_14 (and_14_out, T4, or_4_out);
  not not_3 (not_3_out, I_BIT);
  or or_8 (AC_load, and_15_out, and_16_out, and_17_out);
  or or_9 (mread, and_14_out, T1);
  or or_10 (or_10_out, D5, D0, D1, D2, D6);
  and and_15 (and_15_out, D7, T4, not_3_out, B5);
  and and_16 (and_16_out, T6, D5);
  and and_17 (and_17_out, or_10_out, T5);
  Priority_Encoder priority_encoder_1 (
    .in0(X0), .in1(1'b0), .in2(1'b0), .in3(X3), .in4(X4), .in5(T0), .in6(T2), .in7(1'b0), .out(out_1));  // open: en_in, gs, en_out
  not not_4 (not_4_out, I_BIT);
  and and_18 (and_18_out, B5, T3, not_4_out, D7);
  and and_19 (X3, D4, T4);
  or or_11 (or_11_out, D6, D5, D0, D1, D2);
  and and_20 (and_20_out, D5, T5);
  and and_21 (and_21_out, D2, T5);
  and and_22 (and_22_out, T5, D1);
  and and_23 (and_23_out, T6, D5);
  and and_24 (and_24_out, T5, D0);
  and and_25 (and_25_out, T4, D3);
  and and_26 (and_26_out, T5, D5);
  and and_27 (and_27_out, or_11_out, T4);
  or or_12 (or_12_out, and_21_out, and_20_out);
  Priority_Encoder priority_encoder_2 (
    .in0(1'b0), .in1(or_12_out), .in2(and_22_out), .in3(and_23_out), .in4(and_24_out), .in5(or_13_out),
    .in6(1'b0), .in7(1'b0), .out(out_2));  // open: en_in, gs, en_out
  or or_13 (or_13_out, INC, and_30_out);
  and and_28 (and_28_out, T6, D6);
  or or_14 (X4, and_27_out, T1);
  not not_5 (not_5_out, I_BIT);
  and and_29 (INC, D7, not_5_out, T4, B5);
  and and_30 (and_30_out, T5, D6);
  or or_15 (X0, and_18_out, and_25_out, and_28_out, and_26_out);

  // Other names for the same wires on the sheet: ALU_s[2:0] = out_2; Bus[2:0] = out_1
endmodule
